# Fritzing sketch disco (saved by Fritzing 0.9.2b)
circuit board: 5.93675cm x 2.62848cm
breadboards: 1

parts:
  Raspberry_Pi1 = Raspberry Pi B rev2
  LED1 = LED - 5mm [color="Red (633nm)" package="5 mm [THT]"]
  R1 = Resistor [tolerance=±5% resistance=320 package=THT]
  LED2 = LED - 5mm [color="Green (555nm)" package="5 mm [THT]"]
  R2 = Resistor [tolerance=±5% resistance=320 package=THT]
  LED3 = LED - 5mm [color="Yellow (592nm)" package="5 mm [THT]"]
  R3 = Resistor [tolerance=±5% resistance=320 package=THT]

nets:
  N1: Raspberry_Pi1.GND, R1.Pin_1, R2.Pin_1, R3.Pin_1
  N2: Raspberry_Pi1.GPIO_17, LED1.anode
  N3: Raspberry_Pi1.GPIO_18, LED2.anode
  N4: Raspberry_Pi1.GPIO_27, LED3.anode
  N5: LED1.cathode, R1.Pin_0
  N6: LED2.cathode, R2.Pin_0
  N7: LED3.cathode, R3.Pin_0
