# Fritzing sketch temperature (saved by Fritzing 0.9.2b)
circuit board: 8.46667cm x 5.64444cm
breadboards: 1

parts:
  Pi1 = Adafruit Pi Cobbler
  DS1 = DS18B20 1-Wire Temperature Sensor [part_number=DS18B20]
  R1 = Resistor [tolerance=±5% resistance=4.7 package="0805 [SMD]"]

nets:
  3V3: Pi1.3V3, DS1.VDD, R1.Pin_0
  GND: Pi1.GND, DS1.GND
  N1: Pi1.#4, DS1.DQ, R1.Pin_1

custom parts:
  Adafruit Pi Cobbler: Adafruit Pi Cobbler GPIO Breakout for Raspberry Pi
